# Fritzing sketch fritzing (saved by Fritzing 0.9.3b)
circuit board: 8.46667cm x 5.64444cm
breadboards: 2

parts:
  U1 = ESP32S-HiLetgo [part_number=ESP32S-HiLetgo]
  DRV_1 = DRV 8825 Stepper Motor Carrier, High Current [part_number="DRV 8825"]

nets:
  N1: U1.GND, DRV_1.MS2
  N2: U1.GPIO16, DRV_1.DIRECTION
  N3: U1.GPIO17, DRV_1.STEP
  N4: U1.GPIO5, DRV_1.SLEEP
  N5: U1.GPIO18, DRV_1.RESET
  N6: U1.GPIO19, DRV_1.MS3
  N7: U1.GPIO21, DRV_1.MS1
  N8: U1.GPIO3, DRV_1.ENABLE

custom parts:
  ESP32S-HiLetgo: HiLetgo ESP-WROOM-32 ESP32 ESP-32S Development Board 2.4GHz Dual-Mode WiFi + Bluetooth Dual Cores Microcontroller The ESP32 integrated with Antenna switches, RF Balun, power amplifiers, low-noise amplifiers, filters, and management modules, and the entire solution occupies the least area of PCB. 2.4 GHz Wi-Fi plus Bluetooth dual-mode chip, with TSMC Ultra-low power consumption 40nm technology,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
